# Fritzing sketch UnoR3 (saved by Fritzing 0.9.1b)
breadboards: 1

parts:
  Raspberry_Pi1 = Raspberry Pi B rev2
  Bauteil1 = Arduino Uno (Rev3)
  R2 = Resistor [tolerance=±5% resistance=3.3k package="1206 [SMD]"]
  R3 = Resistor [tolerance=±5% resistance=1.8k package="1206 [SMD]"]

nets:
  5V: Raspberry_Pi1.5V, Bauteil1.5V
  GND: Raspberry_Pi1.GND, Bauteil1.GND, R2.Pin_1
  N1: Raspberry_Pi1.GPIO_14, Bauteil1.D0/RX
  N2: Raspberry_Pi1.GPIO_15, R2.Pin_0, R3.Pin_1
  N3: Raspberry_Pi1.GPIO_18, Bauteil1.RESET
  N4: Bauteil1.D1/TX, R3.Pin_0
